// Logisim project e2521748.circ as structural Verilog: 1 circuit, main circuit main
module main (
  input  A1,
  input  A0,
  input  B1,
  input  B0,
  input  O3,
  input  O2,
  input  O1,
  input  O0,
  output G,
  output L,
  output E,
  output S,
  output C,
  output L8,
  output L6,
  output L4,
  output L2,
  output L1,
  output P,
  output L0,
  output Z,
  output L3,
  output L7,
  output L9,
  output L5
);

  wire and_1_out, and_2_out, and_3_out, and_4_out, and_6_out, and_7_out, and_8_out, and_9_out, and_10_out,
       and_11_out, and_12_out, and_13_out, and_14_out, and_15_out, and_16_out, and_17_out, and_18_out,
       and_19_out, and_20_out, and_21_out, and_22_out, and_23_out, and_24_out, and_25_out, and_26_out,
       and_27_out, and_28_out, and_29_out, and_30_out, and_31_out, and_32_out, and_33_out, and_34_out,
       and_35_out, and_36_out, and_37_out, and_38_out, and_39_out, n3_to_8_decoder_74138_1_p4,
       n3_to_8_decoder_74138_1_p5, n3_to_8_decoder_74138_1_p6, n3_to_8_decoder_74138_1_p7,
       n3_to_8_decoder_74138_1_p8, n3_to_8_decoder_74138_1_p9, n3_to_8_decoder_74138_1_p10,
       n3_to_8_decoder_74138_2_p10, n3_to_8_decoder_74138_2_p11, n3_to_8_decoder_74138_2_p12,
       n3_to_8_decoder_74138_2_p13, n3_to_8_decoder_74138_2_p14, n3_to_8_decoder_74138_2_p15,
       n3_to_8_decoder_74138_2_p16, n3_to_8_decoder_74138_2_p17, n3_to_8_decoder_74138_2_p18,
       n3_to_8_decoder_74138_3_p2, n3_to_8_decoder_74138_3_p7, n3_to_8_decoder_74138_3_p8,
       n3_to_8_decoder_74138_3_p9, n3_to_8_decoder_74138_3_p10, n4_to_1_mux_x2_74153_1_p13,
       n4_to_1_mux_x2_74153_1_p14, n4_to_1_mux_x2_74153_2_p8, n4_to_1_mux_x2_74153_2_p13,
       n4_to_1_mux_x2_74153_2_p14, n4_to_1_mux_x2_74153_3_p7, n4_to_1_mux_x2_74153_3_p13,
       n4_to_1_mux_x2_74153_3_p14, n4_to_1_mux_x2_74153_4_p1, n4_to_1_mux_x2_74153_4_p8,
       n4_to_1_mux_x2_74153_4_p13, n4_to_1_mux_x2_74153_4_p14, n4_to_1_mux_x2_74153_5_p8,
       n4_to_1_mux_x2_74153_5_p13, n4_to_1_mux_x2_74153_5_p14, n4_to_1_mux_x2_74153_6_p13,
       n4_to_1_mux_x2_74153_6_p14, n4_to_1_mux_x2_74153_7_p13, n4_to_1_mux_x2_74153_7_p14,
       n4_to_1_mux_x2_74153_8_p13, n4_to_1_mux_x2_74153_8_p14, n4_to_1_mux_x2_74153_9_p13,
       n4_to_1_mux_x2_74153_9_p14, n4_to_1_mux_x2_74153_10_p17, n4_to_1_mux_x2_74153_10_p18,
       n4_to_1_mux_x2_74153_11_p13, n4_to_1_mux_x2_74153_11_p14, n4_to_1_mux_x2_74153_12_p13,
       n4_to_1_mux_x2_74153_12_p14, n4_to_1_mux_x2_74153_13_p13, n4_to_1_mux_x2_74153_13_p14,
       n4_to_1_mux_x2_74153_14_p13, n4_to_1_mux_x2_74153_14_p14, n4_to_1_mux_x2_74153_15_p13,
       n4_to_1_mux_x2_74153_15_p14, not_1_out, not_2_out, not_3_out, not_4_out, not_5_out, not_6_out,
       not_7_out, not_8_out, not_9_out, not_10_out, not_11_out, not_12_out, not_13_out, not_14_out,
       not_15_out, not_16_out, not_17_out, not_18_out, not_19_out, not_20_out, not_21_out, not_22_out,
       not_23_out, not_24_out, not_25_out, not_26_out, not_27_out, not_28_out, not_30_out, not_31_out,
       not_32_out, not_33_out, not_34_out, not_35_out, not_36_out, not_37_out, not_38_out, not_39_out,
       not_40_out, not_41_out, not_42_out, not_43_out, not_48_out, not_49_out, not_50_out, not_51_out,
       not_52_out, not_53_out, not_54_out, not_55_out, not_56_out, not_57_out, not_58_out, not_59_out,
       not_60_out, or_1_out, or_2_out, or_3_out, or_4_out, or_5_out, or_6_out, or_7_out, or_8_out, or_9_out,
       or_10_out, or_11_out, or_12_out, or_13_out, or_14_out, or_15_out, or_16_out, or_17_out, or_18_out,
       or_19_out, or_20_out, or_21_out, or_22_out, or_23_out, or_24_out, or_25_out, or_26_out, or_27_out,
       or_28_out, or_29_out, or_30_out, or_31_out, or_32_out, or_33_out, or_34_out, or_35_out, or_36_out,
       or_37_out, or_38_out, or_39_out, or_40_out, or_41_out, or_42_out, or_43_out, or_44_out, or_45_out,
       or_46_out, or_47_out, or_48_out, or_49_out, or_50_out, or_51_out, or_52_out, or_53_out, or_54_out,
       or_57_out, or_58_out, or_59_out, or_60_out, or_61_out, or_62_out, or_64_out, or_66_out, or_67_out,
       or_68_out, or_69_out, xnor_1_out, xnor_2_out, xor_1_out, xor_2_out;

  not not_1 (not_1_out, A1);
  not not_2 (not_2_out, A1);
  and and_1 (and_1_out, not_2_out, B1);
  and and_2 (and_2_out, not_4_out, 1'b1);
  or or_1 (or_1_out, and_1_out, and_2_out);
  or or_2 (or_2_out, or_1_out, not_5_out);
  and and_3 (and_3_out, not_1_out, B1);
  // _3_to_8_decoder__74138 #(.Facing("east")) 3_to_8_decoder_74138_1: pin names not known; wires that end beside it: B0, B1, A0, n3_to_8_decoder_74138_1_p4, n3_to_8_decoder_74138_1_p5, n3_to_8_decoder_74138_1_p6, n3_to_8_decoder_74138_1_p7, n3_to_8_decoder_74138_1_p8, n3_to_8_decoder_74138_1_p9, n3_to_8_decoder_74138_1_p10
  not not_3 (not_3_out, A1);
  // _3_to_8_decoder__74138 #(.Facing("east")) 3_to_8_decoder_74138_2: pin names not known; wires that end beside it: B0, B1, A0, not_3_out, A1, 1'b0, 1'b0, 1'b0, 1'b0, n3_to_8_decoder_74138_2_p10, n3_to_8_decoder_74138_2_p11, n3_to_8_decoder_74138_2_p12, n3_to_8_decoder_74138_2_p13, n3_to_8_decoder_74138_2_p14, n3_to_8_decoder_74138_2_p15, n3_to_8_decoder_74138_2_p16, n3_to_8_decoder_74138_2_p17, n3_to_8_decoder_74138_2_p18
  or or_3 (or_3_out, or_2_out, not_15_out);
  or or_4 (or_4_out, A1, B1);
  or or_5 (or_5_out, A0, B0);
  not not_4 (not_4_out, n3_to_8_decoder_74138_1_p4);
  not not_5 (not_5_out, n3_to_8_decoder_74138_1_p5);
  not not_6 (not_6_out, n3_to_8_decoder_74138_1_p6);
  not not_7 (not_7_out, n3_to_8_decoder_74138_1_p7);
  not not_8 (not_8_out, n3_to_8_decoder_74138_1_p8);
  not not_9 (not_9_out, n3_to_8_decoder_74138_1_p9);
  not not_10 (not_10_out, n3_to_8_decoder_74138_1_p10);
  not not_11 (not_11_out, n3_to_8_decoder_74138_2_p10);
  not not_12 (not_12_out, n3_to_8_decoder_74138_2_p11);
  not not_13 (not_13_out, n3_to_8_decoder_74138_2_p12);
  not not_14 (not_14_out, n3_to_8_decoder_74138_2_p13);
  not not_15 (not_15_out, n3_to_8_decoder_74138_2_p14);
  not not_16 (not_16_out, n3_to_8_decoder_74138_2_p15);
  not not_17 (not_17_out, n3_to_8_decoder_74138_2_p16);
  not not_18 (not_18_out, n3_to_8_decoder_74138_2_p17);
  not not_19 (not_19_out, n3_to_8_decoder_74138_2_p18);
  or or_6 (or_6_out, and_3_out, not_15_out);
  or or_7 (or_7_out, not_11_out, not_14_out);
  or or_8 (or_8_out, not_6_out, not_11_out);
  or or_9 (or_9_out, not_5_out, not_8_out);
  or or_10 (or_10_out, not_10_out, not_13_out);
  or or_11 (or_11_out, not_4_out, not_5_out);
  or or_12 (or_12_out, not_6_out, not_7_out);
  or or_13 (or_13_out, not_4_out, not_9_out);
  or or_14 (or_14_out, not_7_out, not_16_out);
  or or_15 (or_15_out, not_5_out, or_6_out);
  and and_4 (and_4_out, B0, A0);
  or or_16 (or_16_out, or_7_out, not_17_out);
  or or_17 (or_17_out, not_6_out, not_9_out);
  or or_18 (or_18_out, not_12_out, not_17_out);
  or or_19 (or_19_out, or_9_out, or_10_out);
  or or_20 (or_20_out, not_15_out, not_18_out);
  or or_21 (or_21_out, not_9_out, not_14_out);
  or or_22 (or_22_out, not_18_out, not_19_out);
  or or_23 (or_23_out, not_5_out, not_8_out);
  or or_24 (or_24_out, or_13_out, or_25_out);
  or or_25 (or_25_out, not_14_out, not_19_out);
  or or_26 (or_26_out, not_7_out, not_10_out);
  or or_27 (or_27_out, not_13_out, not_16_out);
  or or_28 (or_28_out, not_18_out, not_15_out);
  // _3_to_8_decoder__74138 #(.Facing("east")) 3_to_8_decoder_74138_3: pin names not known; wires that end beside it: and_4_out, n3_to_8_decoder_74138_3_p2, 1'b0, 1'b1, 1'b0, 1'b0, n3_to_8_decoder_74138_3_p7, n3_to_8_decoder_74138_3_p8, n3_to_8_decoder_74138_3_p9, n3_to_8_decoder_74138_3_p10
  and and_5 (n3_to_8_decoder_74138_3_p2, A1, B1);
  or or_29 (or_29_out, or_17_out, not_12_out);
  or or_30 (or_30_out, or_8_out, or_18_out);
  or or_31 (or_31_out, or_19_out, or_20_out);
  or or_32 (or_32_out, or_21_out, or_22_out);
  or or_33 (or_33_out, not_8_out, or_34_out);
  or or_34 (or_34_out, or_11_out, or_12_out);
  or or_35 (or_35_out, not_12_out, not_16_out);
  or or_36 (or_36_out, or_26_out, or_27_out);
  // _3_to_8_decoder__74138 #(.Facing("east")) 3_to_8_decoder_74138_4: pin names not known; wires that end beside it: or_5_out, or_4_out, 1'b0, 1'b1, 1'b0, 1'b0
  or or_37 (or_37_out, not_10_out, not_13_out);
  or or_38 (or_38_out, not_10_out, not_11_out);
  not not_20 (not_20_out, n3_to_8_decoder_74138_3_p9);
  not not_21 (not_21_out, n3_to_8_decoder_74138_3_p10);
  or or_39 (or_39_out, or_33_out, or_35_out);
  // NOT_Gate not_22 has open pins: in=open, out=not_22_out
  // NOT_Gate not_23 has open pins: in=open, out=not_23_out
  // NOT_Gate not_24 has open pins: in=open, out=not_24_out
  // NOT_Gate not_25 has open pins: in=open, out=not_25_out
  or or_40 (or_40_out, not_11_out, not_17_out);
  or or_41 (or_41_out, or_38_out, not_18_out);
  not not_26 (not_26_out, n3_to_8_decoder_74138_3_p8);
  not not_27 (not_27_out, n3_to_8_decoder_74138_3_p7);
  // _4_to_1_MUX__x2___74153 #(.Facing("east")) 4_to_1_mux_x2_74153_1: pin names not known; wires that end beside it: 1'b0, 1'b0, 1'b0, or_28_out, 1'b0, 1'b0, 1'b0, 1'b0, 1'b0, O0, 1'b0, O1, n4_to_1_mux_x2_74153_1_p13, n4_to_1_mux_x2_74153_1_p14
  or or_42 (or_42_out, or_41_out, not_15_out);
  // _4_to_1_MUX__x2___74153 #(.Facing("east")) 4_to_1_mux_x2_74153_2: pin names not known; wires that end beside it: not_15_out, or_37_out, not_13_out, or_29_out, or_30_out, 1'b0, not_20_out, n4_to_1_mux_x2_74153_2_p8, 1'b0, O0, 1'b0, O1, n4_to_1_mux_x2_74153_2_p13, n4_to_1_mux_x2_74153_2_p14
  // _4_to_1_MUX__x2___74153 #(.Facing("east")) 4_to_1_mux_x2_74153_3: pin names not known; wires that end beside it: or_41_out, not_9_out, or_32_out, or_23_out, or_31_out, not_26_out, n4_to_1_mux_x2_74153_3_p7, 1'b0, 1'b0, O0, 1'b0, O1, n4_to_1_mux_x2_74153_3_p13, n4_to_1_mux_x2_74153_3_p14
  // _4_to_1_MUX__x2___74153 #(.Facing("east")) 4_to_1_mux_x2_74153_4: pin names not known; wires that end beside it: n4_to_1_mux_x2_74153_4_p1, or_39_out, or_3_out, not_4_out, or_24_out, 1'b0, not_27_out, n4_to_1_mux_x2_74153_4_p8, 1'b0, O0, 1'b0, O1, n4_to_1_mux_x2_74153_4_p13, n4_to_1_mux_x2_74153_4_p14
  // _4_to_1_MUX__x2___74153 #(.Facing("east")) 4_to_1_mux_x2_74153_5: pin names not known; wires that end beside it: 1'b0, or_40_out, not_17_out, or_36_out, or_14_out, 1'b0, not_21_out, n4_to_1_mux_x2_74153_5_p8, 1'b0, O0, 1'b0, O1, n4_to_1_mux_x2_74153_5_p13, n4_to_1_mux_x2_74153_5_p14
  // _4_to_1_MUX__x2___74153 #(.Facing("east")) 4_to_1_mux_x2_74153_6: pin names not known; wires that end beside it: 1'b0, 1'b0, 1'b0, 1'b0, 1'b0, 1'b0, 1'b0, 1'b0, 1'b0, O0, 1'b0, O1, n4_to_1_mux_x2_74153_6_p13, n4_to_1_mux_x2_74153_6_p14
  // _4_to_1_MUX__x2___74153 #(.Facing("east")) 4_to_1_mux_x2_74153_7: pin names not known; wires that end beside it: 1'b0, not_19_out, 1'b0, 1'b0, 1'b0, 1'b0, 1'b0, 1'b0, 1'b0, O0, 1'b0, O1, n4_to_1_mux_x2_74153_7_p13, n4_to_1_mux_x2_74153_7_p14
  and and_6 (and_6_out, n4_to_1_mux_x2_74153_7_p14, O2);
  and and_7 (and_7_out, n4_to_1_mux_x2_74153_1_p14, O2);
  not not_28 (not_28_out, B1);
  or or_43 (or_43_out, not_15_out, not_18_out);
  not not_29 (n4_to_1_mux_x2_74153_4_p1, or_42_out);
  and and_8 (and_8_out, n4_to_1_mux_x2_74153_2_p14, O2);
  or or_44 (or_44_out, and_8_out, and_18_out);
  and and_9 (and_9_out, n4_to_1_mux_x2_74153_3_p14, O2);
  and and_10 (and_10_out, n4_to_1_mux_x2_74153_4_p14, O2);
  or or_45 (or_45_out, and_10_out, and_20_out);
  not not_30 (not_30_out, O2);
  and and_11 (and_11_out, n4_to_1_mux_x2_74153_5_p13, not_30_out);
  and and_12 (and_12_out, n4_to_1_mux_x2_74153_5_p14, O2);
  or or_46 (or_46_out, and_12_out, and_11_out);
  not not_31 (not_31_out, O2);
  and and_13 (and_13_out, n4_to_1_mux_x2_74153_6_p13, not_31_out);
  and and_14 (and_14_out, n4_to_1_mux_x2_74153_6_p14, O2);
  or or_47 (or_47_out, and_14_out, and_13_out);
  not not_32 (not_32_out, O2);
  and and_15 (and_15_out, n4_to_1_mux_x2_74153_7_p13, not_32_out);
  or or_48 (or_48_out, and_6_out, and_15_out);
  not not_33 (not_33_out, O2);
  and and_16 (and_16_out, n4_to_1_mux_x2_74153_1_p13, not_33_out);
  or or_49 (or_49_out, and_7_out, and_16_out);
  and and_17 (and_17_out, A1, not_28_out);
  or or_50 (or_50_out, not_8_out, not_18_out);
  not not_34 (not_34_out, O2);
  and and_18 (and_18_out, n4_to_1_mux_x2_74153_2_p13, not_34_out);
  not not_35 (not_35_out, O2);
  and and_19 (and_19_out, n4_to_1_mux_x2_74153_3_p13, not_35_out);
  or or_51 (or_51_out, and_9_out, and_19_out);
  not not_36 (not_36_out, O2);
  and and_20 (and_20_out, n4_to_1_mux_x2_74153_4_p13, not_36_out);
  assign L3 = O3 ? not_25_out : 1'bz;  // Controlled_Buffer controlled_buffer_1
  assign L7 = O3 ? 1'b0 : 1'bz;  // Controlled_Buffer controlled_buffer_2
  assign L9 = O3 ? 1'b0 : 1'bz;  // Controlled_Buffer controlled_buffer_3
  assign L5 = O3 ? 1'b0 : 1'bz;  // Controlled_Buffer controlled_buffer_4
  or or_52 (or_52_out, and_17_out, or_50_out);
  assign L3 = not_37_out ? or_46_out : 1'bz;  // Controlled_Buffer controlled_buffer_5
  not not_37 (not_37_out, O3);
  assign L7 = not_38_out ? or_47_out : 1'bz;  // Controlled_Buffer controlled_buffer_6
  not not_38 (not_38_out, O3);
  assign L9 = not_39_out ? or_48_out : 1'bz;  // Controlled_Buffer controlled_buffer_7
  not not_39 (not_39_out, O3);
  assign L5 = not_40_out ? or_49_out : 1'bz;  // Controlled_Buffer controlled_buffer_8
  not not_40 (not_40_out, O3);
  and and_21 (and_21_out, A1, B1);
  or or_53 (or_53_out, not_11_out, not_17_out);
  xor xor_1 (xor_1_out, A1, B1);
  xor xor_2 (xor_2_out, A0, B0);
  assign L1 = not_41_out ? or_51_out : 1'bz;  // Controlled_Buffer controlled_buffer_9
  not not_41 (not_41_out, O3);
  assign L1 = O3 ? not_23_out : 1'bz;  // Controlled_Buffer controlled_buffer_10
  assign L0 = not_42_out ? or_45_out : 1'bz;  // Controlled_Buffer controlled_buffer_11
  not not_42 (not_42_out, O3);
  assign L0 = O3 ? not_22_out : 1'bz;  // Controlled_Buffer controlled_buffer_12
  // _4_to_1_MUX__x2___74153 #(.Facing("east")) 4_to_1_mux_x2_74153_8: pin names not known; wires that end beside it: 1'b0, 1'b0, 1'b0, 1'b0, or_15_out, 1'b0, 1'b0, 1'b0, 1'b0, O0, 1'b0, O1, n4_to_1_mux_x2_74153_8_p13, n4_to_1_mux_x2_74153_8_p14
  or or_54 (or_54_out, and_21_out, or_53_out);
  // _3_to_8_decoder__74138 #(.Facing("east")) 3_to_8_decoder_74138_5: pin names not known; wires that end beside it: xor_2_out, xor_1_out, 1'b0, 1'b1, 1'b0, 1'b0
  not not_43 (not_43_out, O2);
  and and_22 (and_22_out, n4_to_1_mux_x2_74153_8_p13, not_43_out);
  and and_23 (and_23_out, n4_to_1_mux_x2_74153_8_p14, O2);
  or or_55 (S, and_23_out, and_22_out);
  // NOT_Gate not_44 has open pins: in=open, out=n4_to_1_mux_x2_74153_4_p8
  // NOT_Gate not_45 has open pins: in=open, out=n4_to_1_mux_x2_74153_3_p7
  // NOT_Gate not_46 has open pins: in=open, out=n4_to_1_mux_x2_74153_2_p8
  // NOT_Gate not_47 has open pins: in=open, out=n4_to_1_mux_x2_74153_5_p8
  // _4_to_1_MUX__x2___74153 #(.Facing("east")) 4_to_1_mux_x2_74153_9: pin names not known; wires that end beside it: 1'b0, 1'b0, 1'b0, or_54_out, 1'b0, 1'b0, 1'b0, 1'b0, 1'b0, O0, 1'b0, O1, n4_to_1_mux_x2_74153_9_p13, n4_to_1_mux_x2_74153_9_p14
  // _4_to_1_MUX__x2___74153 #(.Facing("east")) 4_to_1_mux_x2_74153_10: pin names not known; wires that end beside it: A1, A0, B1, B0, 1'b0, 1'b0, 1'b0, 1'b0, 1'b0, 1'b0, 1'b0, 1'b0, 1'b0, O0, 1'b0, O1, n4_to_1_mux_x2_74153_10_p17, n4_to_1_mux_x2_74153_10_p18
  // _4_to_1_MUX__x2___74153 #(.Facing("east")) 4_to_1_mux_x2_74153_11: pin names not known; wires that end beside it: 1'b0, or_43_out, 1'b0, not_19_out, 1'b0, 1'b0, 1'b0, 1'b0, 1'b0, O0, 1'b0, O1, n4_to_1_mux_x2_74153_11_p13, n4_to_1_mux_x2_74153_11_p14
  // _4_to_1_MUX__x2___74153 #(.Facing("east")) 4_to_1_mux_x2_74153_12: pin names not known; wires that end beside it: 1'b0, not_14_out, 1'b0, or_16_out, 1'b0, 1'b0, 1'b0, 1'b0, 1'b0, O0, 1'b0, O1, n4_to_1_mux_x2_74153_12_p13, n4_to_1_mux_x2_74153_12_p14
  assign L2 = O3 ? not_24_out : 1'bz;  // Controlled_Buffer controlled_buffer_13
  not not_48 (not_48_out, O2);
  and and_24 (and_24_out, n4_to_1_mux_x2_74153_9_p14, O2);
  and and_25 (and_25_out, n4_to_1_mux_x2_74153_9_p13, not_48_out);
  or or_56 (C, and_24_out, and_25_out);
  not not_49 (not_49_out, O2);
  and and_26 (and_26_out, n4_to_1_mux_x2_74153_10_p18, O2);
  and and_27 (and_27_out, n4_to_1_mux_x2_74153_10_p17, not_49_out);
  or or_57 (or_57_out, and_26_out, and_27_out);
  not not_50 (not_50_out, O2);
  and and_28 (and_28_out, n4_to_1_mux_x2_74153_11_p14, O2);
  and and_29 (and_29_out, n4_to_1_mux_x2_74153_11_p13, not_50_out);
  or or_58 (or_58_out, and_28_out, and_29_out);
  not not_51 (not_51_out, O2);
  and and_30 (and_30_out, n4_to_1_mux_x2_74153_12_p13, not_51_out);
  and and_31 (and_31_out, n4_to_1_mux_x2_74153_12_p14, O2);
  or or_59 (or_59_out, and_31_out, and_30_out);
  assign L2 = not_52_out ? or_44_out : 1'bz;  // Controlled_Buffer controlled_buffer_14
  not not_52 (not_52_out, O3);
  not not_53 (not_53_out, O3);
  assign L8 = O3 ? 1'b0 : 1'bz;  // Controlled_Buffer controlled_buffer_15
  assign L6 = not_54_out ? or_58_out : 1'bz;  // Controlled_Buffer controlled_buffer_16
  not not_54 (not_54_out, O3);
  assign L6 = O3 ? 1'b0 : 1'bz;  // Controlled_Buffer controlled_buffer_17
  assign L4 = not_55_out ? or_59_out : 1'bz;  // Controlled_Buffer controlled_buffer_18
  not not_55 (not_55_out, O3);
  assign L4 = O3 ? 1'b0 : 1'bz;  // Controlled_Buffer controlled_buffer_19
  xnor xnor_1 (xnor_1_out, A1, B1);
  xnor xnor_2 (xnor_2_out, A0, B0);
  assign L8 = not_53_out ? or_57_out : 1'bz;  // Controlled_Buffer controlled_buffer_20
  and and_32 (and_32_out, xnor_1_out, xnor_2_out);
  // _4_to_1_MUX__x2___74153 #(.Facing("east")) 4_to_1_mux_x2_74153_13: pin names not known; wires that end beside it: 1'b0, 1'b0, 1'b0, 1'b0, 1'b0, and_32_out, 1'b0, 1'b0, 1'b0, O0, 1'b0, O1, n4_to_1_mux_x2_74153_13_p13, n4_to_1_mux_x2_74153_13_p14
  or or_60 (or_60_out, L3, L0);
  and and_33 (and_33_out, n4_to_1_mux_x2_74153_13_p14, O2);
  not not_56 (not_56_out, or_52_out);
  not not_57 (not_57_out, and_32_out);
  or or_61 (or_61_out, L6, L5);
  or or_62 (or_62_out, or_61_out, or_60_out);
  not not_58 (not_58_out, O2);
  and and_34 (and_34_out, n4_to_1_mux_x2_74153_13_p13, not_58_out);
  or or_63 (E, and_33_out, and_34_out);
  and and_35 (and_35_out, not_56_out, not_57_out);
  or or_64 (or_64_out, L9, or_62_out);
  // _4_to_1_MUX__x2___74153 #(.Facing("east")) 4_to_1_mux_x2_74153_14: pin names not known; wires that end beside it: 1'b0, 1'b0, 1'b0, 1'b0, 1'b0, or_52_out, 1'b0, 1'b0, 1'b0, O0, 1'b0, O1, n4_to_1_mux_x2_74153_14_p13, n4_to_1_mux_x2_74153_14_p14
  not not_59 (not_59_out, O2);
  and and_36 (and_36_out, n4_to_1_mux_x2_74153_14_p13, not_59_out);
  and and_37 (and_37_out, n4_to_1_mux_x2_74153_14_p14, O2);
  or or_65 (G, and_37_out, and_36_out);
  or or_66 (or_66_out, L8, L7);
  or or_67 (or_67_out, or_68_out, or_66_out);
  assign P = or_64_out ? 1'b0 : 1'bz;  // Controlled_Buffer controlled_buffer_21
  // _4_to_1_MUX__x2___74153 #(.Facing("east")) 4_to_1_mux_x2_74153_15: pin names not known; wires that end beside it: 1'b0, 1'b0, 1'b0, 1'b0, 1'b0, and_35_out, 1'b0, 1'b0, 1'b0, O0, 1'b0, O1, n4_to_1_mux_x2_74153_15_p13, n4_to_1_mux_x2_74153_15_p14, O0, O1, O2
  or or_68 (or_68_out, L4, L2);
  or or_69 (or_69_out, or_67_out, L1);
  not not_60 (not_60_out, O2);
  and and_38 (and_38_out, n4_to_1_mux_x2_74153_15_p14, O2);
  and and_39 (and_39_out, n4_to_1_mux_x2_74153_15_p13, not_60_out);
  or or_70 (L, and_38_out, and_39_out);
  assign P = or_69_out ? 1'b1 : 1'bz;  // Controlled_Buffer controlled_buffer_22

  assign Z = L0;
endmodule
